// Logisim project subtask_three_22101071.circ as structural Verilog: 1 circuit, main circuit main
module main (
);

  wire and_1_out, and_2_out, and_3_out, and_4_out, and_5_out, and_6_out, and_7_out, and_8_out, and_9_out,
       and_10_out, button_1_out, button_2_out, button_3_out, button_4_out, button_5_out, button_6_out,
       button_7_out, button_8_out, not_1_out, not_2_out, not_3_out, or_1_out, or_2_out, or_3_out, or_4_out,
       or_5_out, or_6_out, or_7_out, or_8_out;
  wire [2:0] priority_encoder_1_out;

  Button button_1 (.out(button_1_out));
  Button button_2 (.out(button_2_out));
  Button button_3 (.out(button_3_out));
  Button button_4 (.out(button_4_out));
  Button button_5 (.out(button_5_out));
  Button button_6 (.out(button_6_out));
  Button button_7 (.out(button_7_out));
  Button button_8 (.out(button_8_out));
  Priority_Encoder priority_encoder_1 (
    .in0(button_1_out), .in1(button_2_out), .in2(button_3_out), .in3(button_4_out), .in4(button_5_out),
    .in5(button_6_out), .in6(button_7_out), .in7(button_8_out), .out(priority_encoder_1_out));  // open: en_in, gs, en_out
  not not_1 (not_1_out, priority_encoder_1_out[1]);
  not not_2 (not_2_out, priority_encoder_1_out[0]);
  not not_3 (not_3_out, priority_encoder_1_out[2]);
  and and_1 (and_1_out, priority_encoder_1_out[0], priority_encoder_1_out[2]);
  and and_2 (and_2_out, not_3_out, not_2_out);
  and and_3 (and_3_out, priority_encoder_1_out[2], priority_encoder_1_out[0], not_1_out);
  and and_4 (and_4_out, priority_encoder_1_out[0], not_3_out, priority_encoder_1_out[1]);
  and and_5 (and_5_out, not_1_out, not_3_out, priority_encoder_1_out[0]);
  and and_6 (and_6_out, not_1_out, not_2_out, not_3_out);
  and and_7 (and_7_out, not_2_out, priority_encoder_1_out[1], not_3_out);
  and and_8 (and_8_out, not_2_out, priority_encoder_1_out[1], priority_encoder_1_out[2]);
  and and_9 (and_9_out, not_2_out, not_1_out, priority_encoder_1_out[2]);
  and and_10 (and_10_out, priority_encoder_1_out[2], priority_encoder_1_out[1], priority_encoder_1_out[0]);
  or or_1 (or_1_out, and_1_out, and_2_out, priority_encoder_1_out[1]);
  or or_2 (or_2_out, and_6_out, and_8_out, and_3_out, and_9_out);
  or or_3 (or_3_out, and_4_out, and_3_out, and_8_out, and_7_out, and_9_out);
  or or_4 (or_4_out, and_6_out, and_7_out, and_8_out);
  or or_5 (or_5_out, and_4_out, and_5_out, and_6_out, and_7_out, and_9_out);
  or or_6 (or_6_out, and_6_out, and_7_out, and_4_out, and_8_out, and_3_out);
  or or_7 (or_7_out, priority_encoder_1_out[0], not_1_out, priority_encoder_1_out[2]);
  _7_Segment_Display u_7_segment_display_1 (
    .g(or_3_out), .f(or_2_out), .a(or_1_out), .b(or_8_out), .e(or_4_out), .d(or_6_out), .c(or_7_out));  // open: dp
  or or_8 (or_8_out, or_5_out, and_10_out);

  // Notes on the sheet:
  //   Button 0
  //   Button 1
  //   Button 2
  //   Button 3
  //   Button 4
  //   Button 5
  //   Button 6
  //   Button 7
endmodule
