// Logisim project subtask_two_22101071.circ as structural Verilog: 1 circuit, main circuit main
module main (
  input  in_1,
  input  in_2,
  input  in_3
);

  wire and_1_out, and_2_out, and_3_out, and_4_out, and_5_out, and_6_out, and_7_out, and_8_out, and_9_out,
       and_10_out, not_1_out, not_2_out, not_3_out, or_1_out, or_2_out, or_3_out, or_4_out, or_5_out,
       or_6_out, or_7_out, or_8_out;

  not not_1 (not_1_out, in_2);
  not not_2 (not_2_out, in_1);
  not not_3 (not_3_out, in_3);
  and and_1 (and_1_out, in_1, in_3);
  and and_2 (and_2_out, not_3_out, not_2_out);
  and and_3 (and_3_out, in_3, in_1, not_1_out);
  and and_4 (and_4_out, in_1, not_3_out, in_2);
  and and_5 (and_5_out, not_1_out, not_3_out, in_1);
  and and_6 (and_6_out, not_1_out, not_2_out, not_3_out);
  and and_7 (and_7_out, not_2_out, in_2, not_3_out);
  and and_8 (and_8_out, not_2_out, in_2, in_3);
  and and_9 (and_9_out, not_2_out, not_1_out, in_3);
  and and_10 (and_10_out, in_3, in_2, in_1);
  or or_1 (or_1_out, and_1_out, and_2_out, in_2);
  or or_2 (or_2_out, and_6_out, and_8_out, and_3_out, and_9_out);
  or or_3 (or_3_out, and_4_out, and_3_out, and_8_out, and_7_out, and_9_out);
  or or_4 (or_4_out, and_6_out, and_7_out, and_8_out);
  or or_5 (or_5_out, and_4_out, and_5_out, and_6_out, and_7_out, and_9_out);
  or or_6 (or_6_out, and_6_out, and_7_out, and_4_out, and_8_out, and_3_out);
  or or_7 (or_7_out, in_1, not_1_out, in_3);
  _7_Segment_Display u_7_segment_display_1 (
    .g(or_3_out), .f(or_2_out), .a(or_1_out), .b(or_8_out), .e(or_4_out), .d(or_6_out), .c(or_7_out));  // open: dp
  or or_8 (or_8_out, or_5_out, and_10_out);

  // Notes on the sheet:
  //   E0'E2'
  //   101
  //   110
  //   100
  //   000
  //   010
  //   011
  //   001
  //   111
  //   E0E2
  //   S2
  //   S1
  //   S5
  //   S6
  //   S3
  //   S4
  //   S7
endmodule
